// Logisim project control.circ as structural Verilog: 1 circuit, main circuit main
module main (
  input  start,
  input  P0eq,
  input  P0lt,
  input  Ceq,
  input  Clt,
  input  CLK,
  output La,
  output Lp,
  output Lc,
  output Sump,
  output Shp,
  output Lr,
  output [2:0] STATE
);

  wire and_1_out, and_2_out, and_3_out, and_4_out, and_5_out, and_6_out, and_7_out, and_8_out, and_9_out,
       and_10_out;
  wire [2:0] N0_out;

  Register #(.width(3)) u_STATE (.D(N0_out), .en(1'b1), .Q(STATE), .clk(CLK));  // open: clr
  and and_1 (and_1_out, ~STATE[2], STATE[1], STATE[0]);  // AND_Gate
  and and_2 (and_2_out, STATE[2], ~STATE[1], ~STATE[0], Ceq);  // AND_Gate
  and and_3 (and_3_out, ~STATE[2], ~STATE[1], STATE[0], P0eq);  // AND_Gate
  and and_4 (and_4_out, ~STATE[2], ~STATE[1], STATE[0], P0lt);  // AND_Gate
  and and_5 (and_5_out, ~STATE[2], STATE[1], ~STATE[0]);  // AND_Gate
  and and_6 (and_6_out, ~STATE[2], ~STATE[1], ~STATE[0], start);  // AND_Gate
  and and_7 (and_7_out, ~STATE[2], ~STATE[1], STATE[0], P0lt);  // AND_Gate
  and and_8 (and_8_out, ~STATE[2], STATE[1], ~STATE[0]);  // AND_Gate
  and and_9 (and_9_out, STATE[2], ~STATE[1], ~STATE[0], Clt);  // AND_Gate
  and and_10 (and_10_out, STATE[2], ~STATE[1], ~STATE[0], Ceq);  // AND_Gate
  or N2 (N0_out[2], and_1_out, and_2_out);
  or N1 (N0_out[1], and_3_out, and_4_out, and_5_out);
  or N0 (N0_out[0], and_6_out, and_7_out, and_8_out, and_9_out, and_10_out);
  and S0 (La, ~STATE[2], ~STATE[1], ~STATE[0]);  // AND_Gate
  and S1 (Lc, ~STATE[2], ~STATE[1], STATE[0]);  // AND_Gate
  and S2 (Sump, ~STATE[2], STATE[1], ~STATE[0]);  // AND_Gate
  and S3 (Shp, ~STATE[2], STATE[1], STATE[0]);  // AND_Gate
  and S5 (Lr, STATE[2], ~STATE[1], STATE[0]);  // AND_Gate
  or or_1 (Lp, La, Sump, Shp, Lr);

  // Notes on the sheet:
  //   P2
  //   P1
  //   P0
endmodule
