// Logisim project datapath.circ as structural Verilog: 4 circuits, main circuit main
module main (
  input  Lc,
  input  [31:0] a_i,
  input  La,
  input  [31:0] b_i,
  input  Sump,
  input  Shp,
  input  Lp,
  input  Lr,
  input  CLK,
  output Ceq,
  output Clt,
  output P0eq,
  output P0lt,
  output [31:0] result_left32,
  output [31:0] result_right32
);

  wire bitselector_1_out;
  wire [6:0] counter_1_q;
  wire [31:0] a_q, multiplexer_1_out, multiplexer_2_out, multiplexer_3_out, multiplexer_4_out,
       multiplexer_5_out, myAdder_result, myShifter_left_result__1_bit_logical_right,
       myShifter_right_result__1_bit_logical_right, product_left_q, product_right__b_q;

  Register #(.width(32)) a (.D(a_i), .en(La), .Q(a_q), .clk(CLK));  // open: clr
  _32_bit_adder myAdder (.a_i(product_left_q), .b_i(a_q), .Cin(1'b0), .result(myAdder_result));  // open: Cout
  Multiplexer #(.width(32), .enable("false")) multiplexer_1 (
    .in0(product_left_q), .in1({32{1'b0}}), .out(multiplexer_1_out), .sel(La));
  Multiplexer #(.width(32), .enable("false")) multiplexer_2 (
    .in0(product_right__b_q), .in1(b_i), .out(multiplexer_2_out), .sel(La));
  Multiplexer #(.width(32), .enable("false")) multiplexer_3 (
    .in0(multiplexer_1_out), .in1(myAdder_result), .out(multiplexer_3_out), .sel(Sump));
  Multiplexer #(.width(32), .enable("false")) multiplexer_4 (
    .in0(multiplexer_2_out), .in1(myShifter_right_result__1_bit_logical_right), .out(multiplexer_4_out),
    .sel(Shp));
  Multiplexer #(.width(32), .enable("false")) multiplexer_5 (
    .in0(multiplexer_3_out), .in1(myShifter_left_result__1_bit_logical_right), .out(multiplexer_5_out),
    .sel(Shp));
  Register #(.width(32)) product_right__b (
    .D(multiplexer_4_out), .en(Lp), .Q(product_right__b_q), .clk(CLK));  // open: clr
  Register #(.width(32)) product_left (.D(multiplexer_5_out), .en(Lp), .Q(product_left_q), .clk(CLK));  // open: clr
  BitSelector #(.width(32)) bitselector_1 (.in(product_right__b_q), .out(bitselector_1_out), .sel({5{1'b0}}));
  Comparator #(.width(1)) comparator_1 (.a(1'b1), .b(bitselector_1_out), .eq(P0eq), .lt(P0lt));  // open: gt
  _64_bit_shifter myShifter (
    .left_input(product_left_q), .right_input(product_right__b_q),
    .left_result__1_bit_logical_right(myShifter_left_result__1_bit_logical_right),
    .right_result__1_bit_logical_right(myShifter_right_result__1_bit_logical_right));
  Counter #(.width(7), .max('h7f), .ongoal("continue")) counter_1 (
    .count(Lc), .Q(counter_1_q), .clk(Lc), .clr(Lr));  // open: load, D, carry
  Comparator #(.width(7)) comparator_2 (.a(counter_1_q), .b(7'b0100000), .eq(Ceq), .lt(Clt));  // open: gt
  Register #(.width(32)) result_reg_left (.D(product_left_q), .en(Lr), .Q(result_left32), .clk(CLK));  // open: clr
  Register #(.width(32)) result_reg_right (
    .D(product_right__b_q), .en(Lr), .Q(result_right32), .clk(CLK));  // open: clr

  // Notes on the sheet:
  //   for counting 32 repetition
endmodule

module fulladder (
  input  c,
  input  a,
  input  b,
  output sum,
  output carry
);

  wire and_1_out, and_2_out, xor_1_out;

  xor xor_1 (xor_1_out, a, b);
  and and_1 (and_1_out, a, b);
  xor xor_2 (sum, xor_1_out, c);
  and and_2 (and_2_out, c, xor_1_out);
  or or_1 (carry, and_2_out, and_1_out);
endmodule

module _32_bit_adder (
  input  [31:0] a_i,
  input  [31:0] b_i,
  input  Cin,
  output Cout,
  output [31:0] result
);

  wire fulladder_1_carry, fulladder_2_carry, fulladder_3_carry, fulladder_4_carry, fulladder_5_carry,
       fulladder_6_carry, fulladder_7_carry, fulladder_8_carry, fulladder_9_carry, fulladder_10_carry,
       fulladder_11_carry, fulladder_12_carry, fulladder_13_carry, fulladder_14_carry, fulladder_15_carry,
       fulladder_16_carry, fulladder_17_carry, fulladder_18_carry, fulladder_19_carry, fulladder_20_carry,
       fulladder_21_carry, fulladder_22_carry, fulladder_23_carry, fulladder_24_carry, fulladder_25_carry,
       fulladder_26_carry, fulladder_27_carry, fulladder_28_carry, fulladder_29_carry, fulladder_30_carry,
       fulladder_31_carry;

  fulladder fulladder_1 (.c(Cin), .a(b_i[0]), .b(a_i[0]), .sum(result[0]), .carry(fulladder_1_carry));
  fulladder fulladder_2 (.c(fulladder_1_carry), .a(a_i[1]), .b(b_i[1]), .sum(result[1]), .carry(fulladder_2_carry));
  fulladder fulladder_3 (.c(fulladder_4_carry), .a(a_i[3]), .b(b_i[3]), .sum(result[3]), .carry(fulladder_3_carry));
  fulladder fulladder_4 (.c(fulladder_2_carry), .a(a_i[2]), .b(b_i[2]), .sum(result[2]), .carry(fulladder_4_carry));
  fulladder fulladder_5 (.c(fulladder_6_carry), .a(a_i[5]), .b(b_i[5]), .sum(result[5]), .carry(fulladder_5_carry));
  fulladder fulladder_6 (.c(fulladder_3_carry), .a(a_i[4]), .b(b_i[4]), .sum(result[4]), .carry(fulladder_6_carry));
  fulladder fulladder_7 (.c(fulladder_5_carry), .a(a_i[6]), .b(b_i[6]), .sum(result[6]), .carry(fulladder_7_carry));
  fulladder fulladder_8 (.c(fulladder_7_carry), .a(a_i[7]), .b(b_i[7]), .sum(result[7]), .carry(fulladder_8_carry));
  fulladder fulladder_9 (.c(fulladder_8_carry), .a(a_i[8]), .b(b_i[8]), .sum(result[8]), .carry(fulladder_9_carry));
  fulladder fulladder_10 (.c(fulladder_9_carry), .a(a_i[9]), .b(b_i[9]), .sum(result[9]), .carry(fulladder_10_carry));
  fulladder fulladder_11 (
    .c(fulladder_10_carry), .a(a_i[10]), .b(b_i[10]), .sum(result[10]), .carry(fulladder_11_carry));
  fulladder fulladder_12 (
    .c(fulladder_11_carry), .a(a_i[11]), .b(b_i[11]), .sum(result[11]), .carry(fulladder_12_carry));
  fulladder fulladder_13 (
    .c(fulladder_14_carry), .a(a_i[13]), .b(b_i[13]), .sum(result[13]), .carry(fulladder_13_carry));
  fulladder fulladder_14 (
    .c(fulladder_12_carry), .a(a_i[12]), .b(b_i[12]), .sum(result[12]), .carry(fulladder_14_carry));
  fulladder fulladder_15 (
    .c(fulladder_16_carry), .a(a_i[15]), .b(b_i[15]), .sum(result[15]), .carry(fulladder_15_carry));
  fulladder fulladder_16 (
    .c(fulladder_13_carry), .a(a_i[14]), .b(b_i[14]), .sum(result[14]), .carry(fulladder_16_carry));
  fulladder fulladder_17 (
    .c(fulladder_18_carry), .a(a_i[17]), .b(b_i[17]), .sum(result[17]), .carry(fulladder_17_carry));
  fulladder fulladder_18 (
    .c(fulladder_15_carry), .a(a_i[16]), .b(b_i[16]), .sum(result[16]), .carry(fulladder_18_carry));
  fulladder fulladder_19 (
    .c(fulladder_17_carry), .a(a_i[18]), .b(b_i[18]), .sum(result[18]), .carry(fulladder_19_carry));
  fulladder fulladder_20 (
    .c(fulladder_19_carry), .a(a_i[19]), .b(b_i[19]), .sum(result[19]), .carry(fulladder_20_carry));
  fulladder fulladder_21 (
    .c(fulladder_22_carry), .a(a_i[21]), .b(b_i[21]), .sum(result[21]), .carry(fulladder_21_carry));
  fulladder fulladder_22 (
    .c(fulladder_20_carry), .a(a_i[20]), .b(b_i[20]), .sum(result[20]), .carry(fulladder_22_carry));
  fulladder fulladder_23 (
    .c(fulladder_24_carry), .a(a_i[23]), .b(b_i[23]), .sum(result[23]), .carry(fulladder_23_carry));
  fulladder fulladder_24 (
    .c(fulladder_21_carry), .a(a_i[22]), .b(b_i[22]), .sum(result[22]), .carry(fulladder_24_carry));
  fulladder fulladder_25 (
    .c(fulladder_26_carry), .a(a_i[25]), .b(b_i[25]), .sum(result[25]), .carry(fulladder_25_carry));
  fulladder fulladder_26 (
    .c(fulladder_23_carry), .a(a_i[24]), .b(b_i[24]), .sum(result[24]), .carry(fulladder_26_carry));
  fulladder fulladder_27 (
    .c(fulladder_28_carry), .a(a_i[27]), .b(b_i[27]), .sum(result[27]), .carry(fulladder_27_carry));
  fulladder fulladder_28 (
    .c(fulladder_25_carry), .a(a_i[26]), .b(b_i[26]), .sum(result[26]), .carry(fulladder_28_carry));
  fulladder fulladder_29 (
    .c(fulladder_27_carry), .a(a_i[28]), .b(b_i[28]), .sum(result[28]), .carry(fulladder_29_carry));
  fulladder fulladder_30 (
    .c(fulladder_29_carry), .a(a_i[29]), .b(b_i[29]), .sum(result[29]), .carry(fulladder_30_carry));
  fulladder fulladder_31 (
    .c(fulladder_30_carry), .a(a_i[30]), .b(b_i[30]), .sum(result[30]), .carry(fulladder_31_carry));
  fulladder fulladder_32 (.c(fulladder_31_carry), .a(a_i[31]), .b(b_i[31]), .sum(result[31]), .carry(Cout));
endmodule

module _64_bit_shifter (
  input  [31:0] left_input,
  input  [31:0] right_input,
  output [31:0] left_result__1_bit_logical_right,
  output [31:0] right_result__1_bit_logical_right
);


  assign left_result__1_bit_logical_right = {1'b0, left_input[31:1]};
  assign right_result__1_bit_logical_right = {left_input[0], right_input[31:1]};

  // Notes on the sheet:
  //   64 bit logical right (1-bit) shifter
endmodule
