// Logisim project mult32.circ as structural Verilog: 1 circuit, main circuit main
module main (
  input  [31:0] a_i,
  input  [31:0] b_i,
  output [31:0] result_left32,
  output [2:0] state,
  output [31:0] result_right32
);

  wire clock_1_out, main_1_la, main_1_lc, main_1_lp, main_1_lr, main_1_shp, main_1_sump, main_2_ceq,
       main_2_clt, main_2_p0eq, main_2_p0lt, start_out;

  Button start (.out(start_out));
  control_main main_1 (
    .start(start_out), .P0eq(main_2_p0eq), .P0lt(main_2_p0lt), .Ceq(main_2_ceq), .Clt(main_2_clt),
    .CLK(clock_1_out), .La(main_1_la), .Lp(main_1_lp), .Lc(main_1_lc), .Sump(main_1_sump), .Shp(main_1_shp),
    .Lr(main_1_lr), .STATE(state));
  Clock clock_1 (.out(clock_1_out));
  datapath_main main_2 (
    .Lc(main_1_lc), .a_i(a_i), .La(main_1_la), .b_i(b_i), .Sump(main_1_sump), .Shp(main_1_shp),
    .Lp(main_1_lp), .Lr(main_1_lr), .CLK(clock_1_out), .Ceq(main_2_ceq), .Clt(main_2_clt),
    .P0eq(main_2_p0eq), .P0lt(main_2_p0lt), .result_left32(result_left32), .result_right32(result_right32));
endmodule
